// Logisim project mips_datapath.circ as structural Verilog: 3 circuits, main circuit main
module main (
);

  wire [31:0] adder_1_out, PC_q;

  Register #(.width(32)) PC (.Q(PC_q));  // open: D, en, clk, clr
  Adder #(.width(32)) adder_1 (.a(32'h4), .b(PC_q), .out(adder_1_out));  // open: cin, cout
  InstructionMemory instructionmemory_1 (.Address(PC_q));  // open: Instruction
endmodule

module InstructionMemory (
  input  [31:0] Address,
  output [31:0] Instruction
);

  ROM #(.addrWidth(24), .dataWidth(32)) rom_1 (.addr(Address[23:0]), .data(Instruction));
endmodule

module RegisterFile (
  input  [31:0] WriteData
);

  Register #(.width(32)) zero (.D(WriteData));  // open: en, clk, Q, clr
  Register #(.width(32)) a0 (.D(WriteData));  // open: en, clk, Q, clr
  Register #(.width(32)) t0 (.D(WriteData));  // open: en, clk, Q, clr
  Register #(.width(32)) t4 (.D(WriteData));  // open: en, clk, Q, clr
  Register #(.width(32)) s0 (.D(WriteData));  // open: en, clk, Q, clr
  Register #(.width(32)) s4 (.D(WriteData));  // open: en, clk, Q, clr
  Register #(.width(32)) t8 (.D(WriteData));  // open: en, clk, Q, clr
  Register #(.width(32)) gp (.D(WriteData));  // open: en, clk, Q, clr
  Register #(.width(32)) at (.D(WriteData));  // open: en, clk, Q, clr
  Register #(.width(32)) a1 ();  // open: D, en, clk, Q, clr
  Register #(.width(32)) t1 ();  // open: D, en, clk, Q, clr
  Register #(.width(32)) t5 ();  // open: D, en, clk, Q, clr
  Register #(.width(32)) s1 ();  // open: D, en, clk, Q, clr
  Register #(.width(32)) s5 ();  // open: D, en, clk, Q, clr
  Register #(.width(32)) t9 (.D(WriteData));  // open: en, clk, Q, clr
  Register #(.width(32)) sp ();  // open: D, en, clk, Q, clr
  Register #(.width(32)) v0 ();  // open: D, en, clk, Q, clr
  Register #(.width(32)) a2 ();  // open: D, en, clk, Q, clr
  Register #(.width(32)) t2 ();  // open: D, en, clk, Q, clr
  Register #(.width(32)) t6 ();  // open: D, en, clk, Q, clr
  Register #(.width(32)) s2 ();  // open: D, en, clk, Q, clr
  Register #(.width(32)) s6 ();  // open: D, en, clk, Q, clr
  Register #(.width(32)) k0 ();  // open: D, en, clk, Q, clr
  Register #(.width(32)) fp ();  // open: D, en, clk, Q, clr
  Register #(.width(32)) v1 ();  // open: D, en, clk, Q, clr
  Register #(.width(32)) a3 ();  // open: D, en, clk, Q, clr
  Register #(.width(32)) t3 ();  // open: D, en, clk, Q, clr
  Register #(.width(32)) t7 ();  // open: D, en, clk, Q, clr
  Register #(.width(32)) s3 ();  // open: D, en, clk, Q, clr
  Register #(.width(32)) s7 ();  // open: D, en, clk, Q, clr
  Register #(.width(32)) k1 ();  // open: D, en, clk, Q, clr
  Register #(.width(32)) ra ();  // open: D, en, clk, Q, clr
endmodule
